# Fritzing sketch car_park (saved by Fritzing 0.9.3b)
breadboards: 1

parts:
  Part1 = Arduino Uno (Rev3)
  M2 = fc-51 [package=THT]
  M3 = fc-51 [package=THT]
  Part2 = LCD1602-I2C
  Part3 = RFID-RC522-v2
  M4 = Dagu DGServo 9g (End View) [part_number=RS001B]

nets:
  N1: Part1.D9_PWM, Part3.RST
  N2: Part1.D10_PWM/SS, Part3.SDA
  N3: Part1.D11_PWM/MOSI, Part3.MOSI
  N4: Part1.D12/MISO, Part3.MISO
  N5: Part1.D13/SCK, Part3.SCK
  N6: Part1.A4/SDA, Part2.SDA
  N7: Part1.A5/SCL, Part2.SCL
  N8: Part1.D3_PWM, M2.pin1
  N9: Part1.D4, M3.pin1
  N10: Part1.D6_PWM, M4.pulse
  3V3: Part1.3V3, Part3.3.3V
  VCC: Part1.5V, M2.pin3, M3.pin3, Part2.VCC, M4.vcc
  GND: Part1.GND, M2.pin2, M3.pin2, Part2.GND, Part3.GND, M4.gnd

custom parts:
  LCD1602-I2C: A standard character display, usually with 2x16 characters. Comes in many colors with LCM1602 IIC attached.
  RFID-RC522-v2: A simple China made RFID-RC522 Reader; do check the pin labels, as this is a MFRC522 based clone.
